// Logisim project ALU_16bit.circ as structural Verilog: 20 circuits, main circuit main
module main (
);

  project_alu project_alu_1 ();  // open: A, B, AUSel, RUSel, OE, AUResult, AUDout, RUResult
endmodule

module LogicUnit_16 (
  input  [15:0] A,
  input  [15:0] B,
  input  [1:0] Selector,
  output [15:0] AND_Out,
  output [15:0] OR_Out,
  output [15:0] XOR_Out,
  output [15:0] Not_Out,
  output [15:0] SelectedOutput
);

  assign AND_Out = A & B;  // AND_Gate and_1, 16 bits wide
  assign OR_Out = A | B;  // OR_Gate or_1, 16 bits wide
  assign XOR_Out = A ^ B;  // XOR_Gate xor_1, 16 bits wide
  assign Not_Out = ~A;  // NOT_Gate not_1, 16 bits wide
  Multiplexer #(.enable("true"), .select(2), .width(16)) multiplexer_1 (
    .in0(AND_Out), .in1(OR_Out), .in2(XOR_Out), .in3(Not_Out), .out(SelectedOutput), .sel(Selector));  // open: en
endmodule

module Incrementor_16 (
  input  [15:0] A,
  output [15:0] Result,
  output Cout
);

  Adder_16 adder_16_1 (.A(A), .B(16'h1), .out_3(Result), .out_4(Cout));
endmodule

module ShiftLeft_16 (
  input  [15:0] A,
  output [15:0] Result
);


  assign Result = {A[13:0], 2'b00};
endmodule

module Complement_16 (
  input  [15:0] A,
  output [15:0] Result,
  output Cout
);

  wire [15:0] not_1_out;

  assign not_1_out = ~A;  // NOT_Gate not_1, 16 bits wide
  Incrementor_16 incrementor_16_1 (.A(not_1_out), .Result(Result), .Cout(Cout));
endmodule

module ShiftRight_16 (
  input  [15:0] A,
  output [15:0] Result
);


  assign Result = {2'b00, A[15:2]};
endmodule

module Modulo_16 (
  input  [15:0] A,
  input  [15:0] B,
  output [15:0] Remainder
);

  Divider #(.width(16)) divider_1 (.a(A), .b(B), .rem(Remainder));  // open: out, upper
endmodule

module Subtractor_16 (
  input  [15:0] A,
  input  [15:0] B,
  output [15:0] out_3,
  output out_4
);

  Subtractor #(.width(16)) subtractor_1 (.a(A), .b(B), .out(out_3), .bin(1'b0), .bout(out_4));
endmodule

module Divider_16 (
  input  [15:0] A,
  input  [15:0] B,
  output [15:0] Quotient,
  output [15:0] Remainder
);

  Divider #(.width(16)) divider_1 (.a(A), .b(B), .out(Quotient), .rem(Remainder));  // open: upper
endmodule

module Multiplier_16 (
  input  [15:0] A,
  input  [15:0] B,
  output [15:0] Quotient
);

  Multiplier #(.width(16)) multiplier_1 (.a(A), .b(B), .out(Quotient));  // open: cin, cout
endmodule

module project_alu (
  input  [15:0] A,
  input  [15:0] B,
  input  [3:0] AUSel,
  input  [2:0] RUSel,
  input  OE,
  output [15:0] AUResult,
  output [15:0] AUDout,
  output RUResult
);

  project_ao project_ao_1 (.A(A), .B(B), .Selector(AUSel), .out_4(AUResult));
  project_ro project_ro_1 (.A(A), .B(B), .Selector(RUSel), .out_4(RUResult));
  assign AUDout = OE ? AUResult : 16'bz;  // Controlled_Buffer controlled_buffer_1
endmodule

module project_ao (
  input  [15:0] A,
  input  [15:0] B,
  input  [3:0] Selector,
  output [15:0] out_4
);

  wire [15:0] adder_16_1_out_3, and_16_1_result, complement_16_1_result, complement_16_2_result,
       divider_16_1_quotient, modulo_16_1_remainder, multiplier_16_1_quotient, or_16_1_result,
       shiftleft_16_1_result, shiftleft_16_2_result, shiftright_16_1_result, shiftright_16_2_result,
       subtractor_16_1_out_3, xor_16_1_result;

  Adder_16 adder_16_1 (.A(A), .B(B), .out_3(adder_16_1_out_3));  // open: out_4
  AND_16 and_16_1 (.A(A), .B(B), .Result(and_16_1_result));
  OR_16 or_16_1 (.A(A), .B(B), .Result(or_16_1_result));
  XOR_16 xor_16_1 (.A(A), .B(B), .Result(xor_16_1_result));
  Divider_16 divider_16_1 (.A(A), .B(B), .Quotient(divider_16_1_quotient));  // open: Remainder
  Modulo_16 modulo_16_1 (.A(A), .B(B), .Remainder(modulo_16_1_remainder));
  Multiplier_16 multiplier_16_1 (.A(A), .B(B), .Quotient(multiplier_16_1_quotient));
  Subtractor_16 subtractor_16_1 (.A(A), .B(B), .out_3(subtractor_16_1_out_3));  // open: out_4
  ShiftLeft_16 shiftleft_16_1 (.A(A), .Result(shiftleft_16_1_result));
  ShiftLeft_16 shiftleft_16_2 (.A(B), .Result(shiftleft_16_2_result));
  ShiftRight_16 shiftright_16_1 (.A(A), .Result(shiftright_16_1_result));
  ShiftRight_16 shiftright_16_2 (.A(B), .Result(shiftright_16_2_result));
  Complement_16 complement_16_1 (.A(A), .Result(complement_16_1_result));  // open: Cout
  Complement_16 complement_16_2 (.A(B), .Result(complement_16_2_result));  // open: Cout
  Multiplexer #(.select(4), .width(16)) multiplexer_1 (
    .in0(adder_16_1_out_3), .in1(and_16_1_result), .in2(or_16_1_result), .in3(xor_16_1_result),
    .in4(divider_16_1_quotient), .in5(modulo_16_1_remainder), .in6(multiplier_16_1_quotient),
    .in7(subtractor_16_1_out_3), .in8(shiftleft_16_1_result), .in9(shiftleft_16_2_result),
    .in10(shiftright_16_1_result), .in11(shiftright_16_2_result), .in12(complement_16_1_result),
    .in13(complement_16_2_result), .out(out_4), .sel(Selector));  // open: in14, in15
endmodule

module AND_16 (
  input  [15:0] A,
  input  [15:0] B,
  output [15:0] Result
);

  assign Result = A & B;  // AND_Gate and_1, 16 bits wide
endmodule

module OR_16 (
  input  [15:0] A,
  input  [15:0] B,
  output [15:0] Result
);

  assign Result = A | B;  // OR_Gate or_1, 16 bits wide
endmodule

module XOR_16 (
  input  [15:0] A,
  input  [15:0] B,
  output [15:0] Result
);

  assign Result = A ^ B;  // XOR_Gate xor_1, 16 bits wide
endmodule

module Adder_16 (
  input  [15:0] A,
  input  [15:0] B,
  output [15:0] out_3,
  output out_4
);

  Adder #(.width(16)) adder_1 (.a(A), .b(B), .out(out_3), .cin(1'b0), .cout(out_4));
endmodule

module project_ro (
  input  [15:0] A,
  input  [15:0] B,
  input  [2:0] Selector,
  output out_4
);

  wire comparator_1_eq, comparator_1_gt, comparator_1_lt, not_1_out, or_1_out, or_2_out;

  Comparator #(.width(16)) comparator_1 (
    .a(A), .b(B), .gt(comparator_1_gt), .eq(comparator_1_eq), .lt(comparator_1_lt));
  or or_1 (or_1_out, comparator_1_gt, comparator_1_eq);
  or or_2 (or_2_out, comparator_1_lt, comparator_1_eq);
  not not_1 (not_1_out, comparator_1_eq);
  Multiplexer #(.select(3)) multiplexer_1 (
    .in0(comparator_1_gt), .in1(comparator_1_eq), .in2(or_1_out), .in3(comparator_1_lt), .in4(or_2_out),
    .in5(not_1_out), .in6(1'b1), .in7(1'b1), .out(out_4), .sel(Selector));

  // Notes on the sheet:
  //   A > B
  //   A & B
  //   A >= B
  //   A < B
  //   A <= B
  //   A != B
endmodule

module Datapath (
  input  [15:0] in_1,
  input  OE_TestingData,
  input  WE_MAR,
  input  RESET_MAR,
  input  OE_MAR,
  input  Internal_OE,
  input  WE_IR,
  input  WE_MBR,
  input  Reset_IR,
  input  RESET_MBR,
  input  OE_IR,
  input  OE_MBR,
  input  WE_A,
  input  WE_OR,
  input  RESET_OR,
  input  Reset_A,
  input  OE_OR,
  input  OE_A,
  input  [3:0] AUSel,
  input  [2:0] RUSel,
  input  OE_AU,
  input  WE_B,
  input  Reset_B,
  input  OE_B,
  output [7:0] Content_MAR,
  output [15:0] Content_IR,
  output [15:0] Content_MBR,
  output [15:0] Dout_IR,
  output [15:0] Content_A,
  output [15:0] Content_Output,
  output [15:0] Dout_A,
  output [15:0] AUResult,
  output [15:0] Dout,
  output RUResult,
  output [15:0] Content_B,
  output [15:0] Dout_B
);

  wire CLK_out;
  wire [7:0] bitselector_1_out, controlled_buffer_6_out;

  Clock CLK (.out(CLK_out));
  Register #(.width(16)) Instruction_Register (.D(Dout), .en(WE_IR), .clk(CLK_out), .Q(Content_IR), .clr(Reset_IR));
  Register #(.width(16)) Register_A (.D(Dout), .en(WE_A), .clk(CLK_out), .Q(Content_A), .clr(Reset_A));
  Register #(.width(16)) Register_B (.D(Dout), .en(WE_B), .clk(CLK_out), .Q(Content_B), .clr(Reset_B));
  assign Dout_IR = OE_IR ? Content_IR : 16'bz;  // Controlled_Buffer controlled_buffer_1
  assign Dout_A = OE_A ? Content_A : 16'bz;  // Controlled_Buffer controlled_buffer_2
  assign Dout_B = OE_B ? Content_B : 16'bz;  // Controlled_Buffer controlled_buffer_3
  BitSelector #(.group(8), .width(16)) bitselector_1 (.in(Dout_IR), .out(bitselector_1_out), .sel(1'b0));
  project_alu project_alu_1 (
    .A(Content_A), .B(Content_B), .AUSel(AUSel), .RUSel(RUSel), .OE(OE_AU), .AUResult(AUResult),
    .AUDout(Dout), .RUResult(RUResult));
  LED D15 (.in(Dout[15]));
  LED D14 (.in(Dout[14]));
  LED D13 (.in(Dout[13]));
  LED D12 (.in(Dout[12]));
  LED D11 (.in(Dout[11]));
  assign Dout = OE_TestingData ? in_1 : 16'bz;  // Controlled_Buffer controlled_buffer_4
  LED D10 (.in(Dout[10]));
  LED D9 (.in(Dout[9]));
  LED D8 (.in(Dout[8]));
  LED D7 (.in(Dout[7]));
  LED D6 (.in(Dout[6]));
  LED D5 (.in(Dout[5]));
  LED D4 (.in(Dout[4]));
  LED D3 (.in(Dout[3]));
  LED D2 (.in(Dout[2]));
  LED D1 (.in(Dout[1]));
  LED D0 (.in(Dout[0]));
  Register Memory_Address_Register (
    .D(bitselector_1_out), .en(WE_MAR), .clk(CLK_out), .Q(Content_MAR), .clr(RESET_MAR));
  assign Dout = Internal_OE ? Content_MBR : 16'bz;  // Controlled_Buffer controlled_buffer_5
  Register #(.width(16)) Memory_Buffer_Register (
    .D(Dout), .en(WE_MBR), .clk(CLK_out), .Q(Content_MBR), .clr(RESET_MBR));
  Register #(.width(16)) Output_Register (.D(Dout), .en(WE_OR), .clk(CLK_out), .Q(Content_Output), .clr(RESET_OR));
  assign controlled_buffer_6_out = OE_MAR ? Content_MAR : 8'bz;  // Controlled_Buffer controlled_buffer_6
  assign Dout = OE_MBR ? Content_MBR : 16'bz;  // Controlled_Buffer controlled_buffer_7
  assign Dout = OE_OR ? Content_Output : 16'bz;  // Controlled_Buffer controlled_buffer_8
  LED led_1 (.in(Dout[15]));
  LED led_2 (.in(Dout[14]));
  LED led_3 (.in(Dout[13]));
  LED led_4 (.in(Dout[12]));
  LED led_5 (.in(Dout[11]));
  LED led_6 (.in(Dout[10]));
  LED led_7 (.in(Dout[9]));
  LED led_8 (.in(Dout[8]));
  LED led_9 (.in(Dout[7]));
  LED led_10 (.in(Dout[6]));
  LED led_11 (.in(Dout[5]));
  LED led_12 (.in(Dout[4]));
  LED led_13 (.in(Dout[3]));
  LED led_14 (.in(Dout[2]));
  LED led_15 (.in(Dout[1]));
  LED led_16 (.in(Dout[0]));
endmodule

module CPU (
  input  [15:0] in_1,
  input  OE_TestingData,
  input  WE_MAR,
  input  Counter_OE,
  input  RESET_MAR,
  input  OE_MAR,
  input  WE_RAM,
  input  Counter_Enable,
  input  Internal_OE,
  input  WE_IR,
  input  OE_RAM,
  input  WE_MBR,
  input  Reset_IR,
  input  RESET_MBR,
  input  OE_IR,
  input  OE_MBR,
  input  WE_A,
  input  Reset_A,
  input  OE_A,
  input  WE_OR,
  input  RESET_OR,
  input  OE_OR,
  input  [3:0] AUSel,
  input  [2:0] RUSel,
  input  OE_AU,
  input  WE_B,
  input  Reset_B,
  input  OE_B,
  output [7:0] Content_MAR,
  output [7:0] Content_Counter,
  output [15:0] Content_IR,
  output [15:0] Content_MBR,
  output [15:0] Dout_IR,
  output [15:0] Content_A,
  output [15:0] Dout_A,
  output [15:0] Content_Output,
  output [15:0] AUResult,
  output [15:0] Dout,
  output RUResult,
  output [15:0] Content_B,
  output [15:0] Dout_B
);

  wire CLK_out;
  wire [7:0] controlled_buffer_1_out, controlled_buffer_7_out;
  wire [15:0] bit_extender_1_out, ram_1_dout;
  wire [31:0] decimaldecoder_1_dout, decimaldecoder_2_dout, decimaldecoder_3_dout, decimaldecoder_4_dout,
       decimaldecoder_5_dout, decimaldecoder_6_dout;

  Clock CLK (.out(CLK_out));
  Counter #(.max('h3)) Program_Counter (
    .count(Counter_Enable), .clk(CLK_out), .D(controlled_buffer_1_out), .Q(Content_Counter));  // open: clr, load, up, carry
  Register #(.width(16)) Instruction_Register (.D(Dout), .en(WE_IR), .clk(CLK_out), .Q(Content_IR), .clr(Reset_IR));
  Register #(.width(16)) Register_A (.D(Dout), .en(WE_A), .clk(CLK_out), .Q(Content_A), .clr(Reset_A));
  Register #(.width(16)) Register_B (.D(Dout), .en(WE_B), .clk(CLK_out), .Q(Content_B), .clr(Reset_B));
  assign controlled_buffer_1_out = Counter_OE ? Content_Counter : 8'bz;  // Controlled_Buffer controlled_buffer_1
  assign Dout_IR = OE_IR ? Content_IR : 16'bz;  // Controlled_Buffer controlled_buffer_2
  assign Dout_A = OE_A ? Content_A : 16'bz;  // Controlled_Buffer controlled_buffer_3
  assign Dout_B = OE_B ? Content_B : 16'bz;  // Controlled_Buffer controlled_buffer_4
  BitSelector #(.group(8), .width(16)) bitselector_1 (.in(Dout_IR), .out(controlled_buffer_1_out), .sel(1'b0));
  assign bit_extender_1_out = {{8{Content_Counter[7]}}, Content_Counter};  // Bit_Extender bit_extender_1
  project_alu project_alu_1 (
    .A(Content_A), .B(Content_B), .AUSel(AUSel), .RUSel(RUSel), .OE(OE_AU), .AUResult(AUResult),
    .AUDout(Dout), .RUResult(RUResult));
  _7_Segment_Display u_7_segment_display_1 (
    .g(decimaldecoder_1_dout[3]), .f(decimaldecoder_1_dout[2]), .a(decimaldecoder_1_dout[1]),
    .b(decimaldecoder_1_dout[0]), .e(decimaldecoder_1_dout[19]), .d(decimaldecoder_1_dout[18]),
    .c(decimaldecoder_1_dout[17]), .dp(decimaldecoder_1_dout[16]));
  DecimalDecoder decimaldecoder_1 (.Din(bit_extender_1_out), .Dout(decimaldecoder_1_dout));
  _7_Segment_Display u_7_segment_display_2 (
    .g(decimaldecoder_2_dout[15]), .f(decimaldecoder_2_dout[14]), .a(decimaldecoder_2_dout[13]),
    .b(decimaldecoder_2_dout[12]), .e(decimaldecoder_2_dout[31]), .d(decimaldecoder_2_dout[30]),
    .c(decimaldecoder_2_dout[29]), .dp(decimaldecoder_2_dout[28]));
  DecimalDecoder decimaldecoder_2 (.Din(Content_IR), .Dout(decimaldecoder_2_dout));
  _7_Segment_Display u_7_segment_display_3 (
    .g(decimaldecoder_2_dout[11]), .f(decimaldecoder_2_dout[10]), .a(decimaldecoder_2_dout[9]),
    .b(decimaldecoder_2_dout[8]), .e(decimaldecoder_2_dout[27]), .d(decimaldecoder_2_dout[26]),
    .c(decimaldecoder_2_dout[25]), .dp(decimaldecoder_2_dout[24]));
  _7_Segment_Display u_7_segment_display_4 (
    .g(decimaldecoder_2_dout[7]), .f(decimaldecoder_2_dout[6]), .a(decimaldecoder_2_dout[5]),
    .b(decimaldecoder_2_dout[4]), .e(decimaldecoder_2_dout[23]), .d(decimaldecoder_2_dout[22]),
    .c(decimaldecoder_2_dout[21]), .dp(decimaldecoder_2_dout[20]));
  DecimalDecoder decimaldecoder_3 (.Din(Content_B), .Dout(decimaldecoder_3_dout));
  _7_Segment_Display u_7_segment_display_5 (
    .g(decimaldecoder_2_dout[3]), .f(decimaldecoder_2_dout[2]), .a(decimaldecoder_2_dout[1]),
    .b(decimaldecoder_2_dout[0]), .e(decimaldecoder_2_dout[19]), .d(decimaldecoder_2_dout[18]),
    .c(decimaldecoder_2_dout[17]), .dp(decimaldecoder_2_dout[16]));
  DecimalDecoder decimaldecoder_4 (.Din(Content_A), .Dout(decimaldecoder_4_dout));
  _7_Segment_Display u_7_segment_display_6 (
    .g(decimaldecoder_3_dout[15]), .f(decimaldecoder_3_dout[14]), .a(decimaldecoder_3_dout[13]),
    .b(decimaldecoder_3_dout[12]), .e(decimaldecoder_3_dout[31]), .d(decimaldecoder_3_dout[30]),
    .c(decimaldecoder_3_dout[29]), .dp(decimaldecoder_3_dout[28]));
  _7_Segment_Display u_7_segment_display_7 (
    .g(decimaldecoder_3_dout[11]), .f(decimaldecoder_3_dout[10]), .a(decimaldecoder_3_dout[9]),
    .b(decimaldecoder_3_dout[8]), .e(decimaldecoder_3_dout[27]), .d(decimaldecoder_3_dout[26]),
    .c(decimaldecoder_3_dout[25]), .dp(decimaldecoder_3_dout[24]));
  _7_Segment_Display u_7_segment_display_8 (
    .g(decimaldecoder_4_dout[15]), .f(decimaldecoder_4_dout[14]), .a(decimaldecoder_4_dout[13]),
    .b(decimaldecoder_4_dout[12]), .e(decimaldecoder_4_dout[31]), .d(decimaldecoder_4_dout[30]),
    .c(decimaldecoder_4_dout[29]), .dp(decimaldecoder_4_dout[28]));
  _7_Segment_Display u_7_segment_display_9 (
    .g(decimaldecoder_4_dout[11]), .f(decimaldecoder_4_dout[10]), .a(decimaldecoder_4_dout[9]),
    .b(decimaldecoder_4_dout[8]), .e(decimaldecoder_4_dout[27]), .d(decimaldecoder_4_dout[26]),
    .c(decimaldecoder_4_dout[25]), .dp(decimaldecoder_4_dout[24]));
  _7_Segment_Display u_7_segment_display_10 (
    .g(decimaldecoder_5_dout[15]), .f(decimaldecoder_5_dout[14]), .a(decimaldecoder_5_dout[13]),
    .b(decimaldecoder_5_dout[12]), .e(decimaldecoder_5_dout[31]), .d(decimaldecoder_5_dout[30]),
    .c(decimaldecoder_5_dout[29]), .dp(decimaldecoder_5_dout[28]));
  DecimalDecoder decimaldecoder_5 (.Din(AUResult), .Dout(decimaldecoder_5_dout));
  _7_Segment_Display u_7_segment_display_11 (
    .g(decimaldecoder_3_dout[7]), .f(decimaldecoder_3_dout[6]), .a(decimaldecoder_3_dout[5]),
    .b(decimaldecoder_3_dout[4]), .e(decimaldecoder_3_dout[23]), .d(decimaldecoder_3_dout[22]),
    .c(decimaldecoder_3_dout[21]), .dp(decimaldecoder_3_dout[20]));
  _7_Segment_Display u_7_segment_display_12 (
    .g(decimaldecoder_3_dout[3]), .f(decimaldecoder_3_dout[2]), .a(decimaldecoder_3_dout[1]),
    .b(decimaldecoder_3_dout[0]), .e(decimaldecoder_3_dout[19]), .d(decimaldecoder_3_dout[18]),
    .c(decimaldecoder_3_dout[17]), .dp(decimaldecoder_3_dout[16]));
  _7_Segment_Display u_7_segment_display_13 (
    .g(decimaldecoder_4_dout[7]), .f(decimaldecoder_4_dout[6]), .a(decimaldecoder_4_dout[5]),
    .b(decimaldecoder_4_dout[4]), .e(decimaldecoder_4_dout[23]), .d(decimaldecoder_4_dout[22]),
    .c(decimaldecoder_4_dout[21]), .dp(decimaldecoder_4_dout[20]));
  _7_Segment_Display u_7_segment_display_14 (
    .g(decimaldecoder_4_dout[3]), .f(decimaldecoder_4_dout[2]), .a(decimaldecoder_4_dout[1]),
    .b(decimaldecoder_4_dout[0]), .e(decimaldecoder_4_dout[19]), .d(decimaldecoder_4_dout[18]),
    .c(decimaldecoder_4_dout[17]), .dp(decimaldecoder_4_dout[16]));
  _7_Segment_Display u_7_segment_display_15 (
    .g(decimaldecoder_5_dout[11]), .f(decimaldecoder_5_dout[10]), .a(decimaldecoder_5_dout[9]),
    .b(decimaldecoder_5_dout[8]), .e(decimaldecoder_5_dout[27]), .d(decimaldecoder_5_dout[26]),
    .c(decimaldecoder_5_dout[25]), .dp(decimaldecoder_5_dout[24]));
  _7_Segment_Display u_7_segment_display_16 (
    .g(decimaldecoder_5_dout[7]), .f(decimaldecoder_5_dout[6]), .a(decimaldecoder_5_dout[5]),
    .b(decimaldecoder_5_dout[4]), .e(decimaldecoder_5_dout[23]), .d(decimaldecoder_5_dout[22]),
    .c(decimaldecoder_5_dout[21]), .dp(decimaldecoder_5_dout[20]));
  _7_Segment_Display u_7_segment_display_17 (
    .g(decimaldecoder_5_dout[3]), .f(decimaldecoder_5_dout[2]), .a(decimaldecoder_5_dout[1]),
    .b(decimaldecoder_5_dout[0]), .e(decimaldecoder_5_dout[19]), .d(decimaldecoder_5_dout[18]),
    .c(decimaldecoder_5_dout[17]), .dp(decimaldecoder_5_dout[16]));
  LED D15 (.in(Dout[15]));
  LED D14 (.in(Dout[14]));
  LED D13 (.in(Dout[13]));
  LED D12 (.in(Dout[12]));
  LED D11 (.in(Dout[11]));
  assign Dout = OE_TestingData ? in_1 : 16'bz;  // Controlled_Buffer controlled_buffer_5
  LED D10 (.in(Dout[10]));
  LED D9 (.in(Dout[9]));
  LED D8 (.in(Dout[8]));
  LED D7 (.in(Dout[7]));
  LED D6 (.in(Dout[6]));
  LED D5 (.in(Dout[5]));
  LED D4 (.in(Dout[4]));
  LED D3 (.in(Dout[3]));
  LED D2 (.in(Dout[2]));
  LED D1 (.in(Dout[1]));
  LED D0 (.in(Dout[0]));
  Register Memory_Address_Register (
    .D(controlled_buffer_1_out), .en(WE_MAR), .clk(CLK_out), .Q(Content_MAR), .clr(RESET_MAR));
  assign Dout = Internal_OE ? Content_MBR : 16'bz;  // Controlled_Buffer controlled_buffer_6
  Register #(.width(16)) Memory_Buffer_Register (
    .D(Dout), .en(WE_MBR), .clk(CLK_out), .Q(Content_MBR), .clr(RESET_MBR));
  Register #(.width(16)) Output_Register (.D(Dout), .en(WE_OR), .clk(CLK_out), .Q(Content_Output), .clr(RESET_OR));
  assign controlled_buffer_7_out = OE_MAR ? Content_MAR : 8'bz;  // Controlled_Buffer controlled_buffer_7
  assign Dout = OE_MBR ? Content_MBR : 16'bz;  // Controlled_Buffer controlled_buffer_8
  assign Dout = OE_OR ? Content_Output : 16'bz;  // Controlled_Buffer controlled_buffer_9
  _7_Segment_Display u_7_segment_display_18 (
    .g(decimaldecoder_6_dout[15]), .f(decimaldecoder_6_dout[14]), .a(decimaldecoder_6_dout[13]),
    .b(decimaldecoder_6_dout[12]), .e(decimaldecoder_6_dout[31]), .d(decimaldecoder_6_dout[30]),
    .c(decimaldecoder_6_dout[29]), .dp(decimaldecoder_6_dout[28]));
  DecimalDecoder decimaldecoder_6 (.Din(Content_Output), .Dout(decimaldecoder_6_dout));
  _7_Segment_Display u_7_segment_display_19 (
    .g(decimaldecoder_6_dout[11]), .f(decimaldecoder_6_dout[10]), .a(decimaldecoder_6_dout[9]),
    .b(decimaldecoder_6_dout[8]), .e(decimaldecoder_6_dout[27]), .d(decimaldecoder_6_dout[26]),
    .c(decimaldecoder_6_dout[25]), .dp(decimaldecoder_6_dout[24]));
  _7_Segment_Display u_7_segment_display_20 (
    .g(decimaldecoder_6_dout[7]), .f(decimaldecoder_6_dout[6]), .a(decimaldecoder_6_dout[5]),
    .b(decimaldecoder_6_dout[4]), .e(decimaldecoder_6_dout[23]), .d(decimaldecoder_6_dout[22]),
    .c(decimaldecoder_6_dout[21]), .dp(decimaldecoder_6_dout[20]));
  LED led_1 (.in(Dout[15]));
  _7_Segment_Display u_7_segment_display_21 (
    .g(decimaldecoder_6_dout[3]), .f(decimaldecoder_6_dout[2]), .a(decimaldecoder_6_dout[1]),
    .b(decimaldecoder_6_dout[0]), .e(decimaldecoder_6_dout[19]), .d(decimaldecoder_6_dout[18]),
    .c(decimaldecoder_6_dout[17]), .dp(decimaldecoder_6_dout[16]));
  LED led_2 (.in(Dout[14]));
  LED led_3 (.in(Dout[13]));
  LED led_4 (.in(Dout[12]));
  LED led_5 (.in(Dout[11]));
  LED led_6 (.in(Dout[10]));
  LED led_7 (.in(Dout[9]));
  LED led_8 (.in(Dout[8]));
  LED led_9 (.in(Dout[7]));
  LED led_10 (.in(Dout[6]));
  LED led_11 (.in(Dout[5]));
  LED led_12 (.in(Dout[4]));
  LED led_13 (.in(Dout[3]));
  LED led_14 (.in(Dout[2]));
  LED led_15 (.in(Dout[1]));
  LED led_16 (.in(Dout[0]));
  RAM #(.clearpin("true"), .dataWidth(16), .enables("line")) ram_1 (
    .addr({controlled_buffer_7_out[0], controlled_buffer_7_out[1], controlled_buffer_7_out[2], controlled_buffer_7_out[3], controlled_buffer_7_out[4], controlled_buffer_7_out[5], controlled_buffer_7_out[6], controlled_buffer_7_out[7]}),
    .we(WE_RAM), .clk(CLK_out), .din(Dout), .dout(ram_1_dout));  // open: clr
  assign Dout = OE_RAM ? ram_1_dout : 16'bz;  // Controlled_Buffer controlled_buffer_10

  // Notes on the sheet:
  //   INTERNAL DATA BUS (8 BITS)
  //   INTERNAL DATA BUS
  //   EXTERNAL DATA BUS (8 BITS)
  //   EXTERNAL DATA BUS
endmodule

module DecimalDecoder (
  input  [15:0] Din,
  output [31:0] Dout
);

  ROM #(.addrWidth(16), .dataWidth(32)) rom_1 (
    .addr(Din),
    .data({Dout[31:28], Dout[15:12], Dout[27:24], Dout[11:8], Dout[23:20], Dout[7:4], Dout[19:16], Dout[3:0]}));

  // Notes on the sheet:
  //   contents of rom_1 (hex, n*v repeats v):
  //   e7 21 cb 6b 2d 6e ee 23 ef 2f 21e7 2121 21cb 216b 212d 216e 21ee 2123 21ef 212f cbe7 cb21 cbcb cb6b
  //   cb2d cb6e cbee cb23 cbef cb2f 6be7 6b21 6bcb 6b6b 6b2d 6b6e 6bee 6b23 6bef 6b2f 2de7 2d21 2dcb 2d6b
  //   2d2d 2d6e 2dee 2d23 2def 2d2f 6ee7 6e21 6ecb 6e6b 6e2d 6e6e 6eee 6e23 6eef 6e2f eee7 ee21 eecb ee6b
  //   ee2d ee6e eeee ee23 eeef ee2f 23e7 2321 23cb 236b 232d 236e 23ee 2323 23ef 232f efe7 ef21 efcb ef6b
  //   ef2d ef6e efee ef23 efef ef2f 2fe7 2f21 2fcb 2f6b 2f2d 2f6e 2fee 2f23 2fef 2f2f 21e7e7 21e721 21e7cb
  //   21e76b 21e72d 21e76e 21e7ee 21e723 21e7ef 21e72f 2121e7 212121 2121cb 21216b 21212d 21216e 2121ee
  //   212123 2121ef 21212f 21cbe7 21cb21 21cbcb 21cb6b 21cb2d 21cb6e 21cbee 21cb23 21cbef 21cb2f 216be7
  //   216b21 216bcb 216b6b 216b2d 216b6e 216bee 216b23 216bef 216b2f 212de7 212d21 212dcb 212d6b 212d2d
  //   212d6e 212dee 212d23 212def 212d2f 216ee7 216e21 216ecb 216e6b 216e2d 216e6e 216eee 216e23 216eef
  //   216e2f 21eee7 21ee21 21eecb 21ee6b 21ee2d 21ee6e 21eeee 21ee23 21eeef 21ee2f 2123e7 212321 2123cb
  //   21236b 21232d 21236e 2123ee 212323 2123ef 21232f 21efe7 21ef21 21efcb 21ef6b 21ef2d 21ef6e 21efee
  //   21ef23 21efef 21ef2f 212fe7 212f21 212fcb 212f6b 212f2d 212f6e 212fee 212f23 212fef 212f2f cbe7e7
  //   cbe721 cbe7cb cbe76b cbe72d cbe76e cbe7ee cbe723 cbe7ef cbe72f cb21e7 cb2121 cb21cb cb216b cb212d
  //   cb216e cb21ee cb2123 cb21ef cb212f cbcbe7 cbcb21 cbcbcb cbcb6b cbcb2d cbcb6e cbcbee cbcb23 cbcbef
  //   cbcb2f cb6be7 cb6b21 cb6bcb cb6b6b cb6b2d cb6b6e cb6bee cb6b23 cb6bef cb6b2f cb2de7 cb2d21 cb2dcb
  //   cb2d6b cb2d2d cb2d6e cb2dee cb2d23 cb2def cb2d2f cb6ee7 cb6e21 cb6ecb cb6e6b cb6e2d cb6e6e
endmodule
